# Fritzing sketch 000 (saved by Fritzing 0.9.3b)
circuit board: 16cm x 10cm
breadboards: 1

parts:
  1_100_2# = Resistor [tolerance=±5% resistance=100 package=THT]  # not connected
  3_330_4# = Resistor [tolerance=±5% resistance=330 package=THT]  # not connected
  5_330_6# = Resistor [tolerance=±5% resistance=330 package=THT]  # not connected
  7_470_8# = Resistor [tolerance=±5% resistance=470 package=THT]  # not connected
  9_470_10# = Resistor [tolerance=±5% resistance=470 package=THT]  # not connected
  11_470_12# = Resistor [tolerance=±5% resistance=470 package=THT]  # not connected
  13_1K_14# = Resistor [tolerance=±5% resistance=1k package=THT]  # not connected
  15_1K_16# = Resistor [tolerance=±5% resistance=1k package=THT]  # not connected
  17_1K_18# = Resistor [tolerance=±5% resistance=1k package=THT]  # not connected
  19_1K_20# = Resistor [tolerance=±5% resistance=1k package=THT]  # not connected
  21_2_2K_22# = Resistor [tolerance=±5% resistance=2.2k package=THT]  # not connected
  23_4_7K_24# = Resistor [tolerance=±5% resistance=4.7k package=THT]  # not connected
  25_4_7K_26# = Resistor [tolerance=±5% resistance=4.7k package=THT]  # not connected
  27_10K_28# = Resistor [tolerance=±5% resistance=10k package=THT]  # not connected
  29_22K_30# = Resistor [tolerance=±5% resistance=22k package=THT]  # not connected
  31_33K_32# = Resistor [tolerance=±5% resistance=33k package=THT]  # not connected
  33_47K_34# = Resistor [tolerance=±5% resistance=47k package=THT]  # not connected
  35_100K_36# = Resistor [tolerance=±5% resistance=100k package=THT]  # not connected
  37_220K_38# = Resistor [tolerance=±5% resistance=220k package=THT]  # not connected
  39_470K_40# = Resistor [tolerance=±5% resistance=470k package=THT]  # not connected
  41_42# = Rectifier Diode [part_number=1N4001 package="300 mil [THT]"]  # not connected
  43_44# = Rectifier Diode [part_number=1N4001 package="300 mil [THT]"]  # not connected
  2K = TRANSFORMER [package=transformer]  # not connected
  4K_CT = female pin header, 1 pin [form="♀ (female)"]  # not connected
  8_OHM = TRANSFORMER [package=transformer]  # not connected
  900CT = female pin header, 1 pin [form="♀ (female)"]  # not connected
  58-1_5V+59# = Screw terminal - 2 pins [package=THT]  # not connected
  59-3V+60# = Screw terminal - 2 pins [package=THT]  # not connected
  58-4_5V+60# = Screw terminal - 2 pins [package=THT]  # not connected
  55-9V+60# = Screw terminal - 2 pins [package=THT]  # not connected
  55-6V+59# = Screw terminal - 2 pins [package=THT]  # not connected
  56-7_5V+60# = Screw terminal - 2 pins [package=THT]  # not connected
  7400 = IC, DIP package, 14 pins [chip_label=IC]  # not connected
  7476 = IC, DIP package, 16 pins [chip_label=IC]  # not connected
  9V_500_OHM = Relay [part_number=FRS1B-S package=THT]  # not connected
  83_82_84# = NPN-Transistor [package="TO92 [THT]"]  # not connected
  80_79_81# = NPN-Transistor [package="TO92 [THT]"]  # not connected
  77_76_78# = PNP-Transistor [package="TO92 [THT]"]  # not connected
  74_73_75# = PNP-Transistor [package="TO92 [THT]"]  # not connected
  71_72# = Rectifier Diode [part_number=1N4001 package="300 mil [THT]"]  # not connected
  85_100pF_86# = Ceramic Capacitor [capacitance=0.1nF package="100 mil [THT, multilayer]"]  # not connected
  87_0_001uF_88# = Ceramic Capacitor [capacitance=1nF package="100 mil [THT, multilayer]"]  # not connected
  89_0_005uF_90# = Ceramic Capacitor [capacitance=5nF package="100 mil [THT, multilayer]"]  # not connected
  91_0_01uF_92# = Ceramic Capacitor [capacitance=10nF package="100 mil [THT, multilayer]"]  # not connected
  93_0_05uF_94# = Ceramic Capacitor [capacitance=50nF package="100 mil [THT, multilayer]"]  # not connected
  95_0_1uF_96# = Ceramic Capacitor [capacitance=100nF package="100 mil [THT, multilayer]"]  # not connected
  97_3_3uF_98# = Electrolytic Capacitor [capacitance=3.3µF package="100 mil [THT, electrolytic]"]  # not connected
  99_10uF_100# = Electrolytic Capacitor [capacitance=10µF package="100 mil [THT, electrolytic]"]  # not connected
  101_100uF_102# = Electrolytic Capacitor [capacitance=100µF package="100 mil [THT, electrolytic]"]  # not connected
  103_100uF_104# = Electrolytic Capacitor [capacitance=100µF package="100 mil [THT, electrolytic]"]  # not connected
  66_67_68_69_70# = female pin header, 5 pins [form="♀ (female)"]  # not connected
  135_136# = Variable Capacitor [capacitance=100nF max_capacitance=265pF min_capacitance=2pF voltage=35V]  # not connected
  137_138_139# = Rotary Potentiometer (Small) [maximum_resistance=50kΩ package=THT]  # not connected
  140_141# = Toggle Switch [package=THT]  # not connected
  142+M-143# = Screw terminal - 2 pins [package=THT]  # not connected
  144_com1 = 7 Segment Display
  145_g_820# = Resistor [tolerance=±5% resistance=820 package=THT]
  146_f_820# = Resistor [tolerance=±5% resistance=820 package=THT]
  147_e_820# = Resistor [tolerance=±5% resistance=820 package=THT]
  820_d_151# = Resistor [tolerance=±5% resistance=820 package=THT]
  820_c_150# = Resistor [tolerance=±5% resistance=820 package=THT]
  820_b_149# = Resistor [tolerance=±5% resistance=820 package=THT]
  820_a_148# = Resistor [tolerance=±5% resistance=820 package=THT]
  152_153# = LED - 5mm [color="Red (633nm)" package="5 mm [THT]"]  # not connected
  154_155# = LED - 5mm [color="Red (633nm)" package="5 mm [THT]"]  # not connected
  156_157# = LED - 5mm [color="Red (633nm)" package="5 mm [THT]"]  # not connected
  158_159# = LED - 5mm [color="Red (633nm)" package="5 mm [THT]"]  # not connected
  160_161# = LED - 5mm [color="Red (633nm)" package="5 mm [THT]"]  # not connected
  162_163# = LED - 5mm [color="Red (633nm)" package="5 mm [THT]"]  # not connected
  164_165_166# = Toggle Switch [package=THT]  # not connected
  167_168# = Pushbutton [package="[THT]"]
  169_170# = LED - 5mm [color="Red (633nm)" package="5 mm [THT]"]  # not connected
  171_172# = PHOTOCELL [package=photocell-kit]  # not connected
  173_174# = Screw terminal - 2 pins [package=THT]  # not connected
  175_176# = Screw terminal - 2 pins [package=THT]  # not connected

nets:
  N1: 144_com1.Segment_G, 145_g_820#.Pin_1
  N2: 144_com1.Segment_F, 146_f_820#.Pin_1
  N3: 144_com1.Segment_E, 147_e_820#.Pin_1
  N4: 144_com1.Segment_D, 820_d_151#.Pin_0
  N5: 144_com1.Segment_C, 820_c_150#.Pin_0
  N6: 144_com1.Segment_B, 820_b_149#.Pin_0
  N7: 144_com1.Segment_A, 820_a_148#.Pin_0
  N8: 167_168#.Pin_1, 167_168#.Pin_2
  N9: 167_168#.Pin_3, 167_168#.Pin_4

notes:
  45 46 47
  48 49
  50 51 52
  53 54
  105 106 107 108 109 110 111
  112 113 114 115 116 117 118
  119 120 121 122 123 124 125 126
  127 128 129 130 131 132 133 134
  63 --- 65
  61 --- 62
  64 --- 64
  com 144
  d
  e
  144 com
  g
  f
  c
  b
  a
  github.com/RebeccaRGB/200in1
  Miss Diode Seal of Approval
  1/200 WHEEL OF FORTUNE
