# Fritzing sketch 001WheelOfFortune (saved by Fritzing 0.9.3b)
circuit board: 7.0012cm x 7cm
breadboards: 1

parts:
  330 = Resistor [tolerance=±5% resistance=330 package=THT]
  470 = Resistor [tolerance=±5% resistance=470 package=THT]
  10K = Resistor [tolerance=±5% resistance=10k package=THT]
  33K = Resistor [tolerance=±5% resistance=33k package=THT]
  47K = Resistor [tolerance=±5% resistance=47k package=THT]
  100K = Resistor [tolerance=±5% resistance=100k package=THT]
  220K = Resistor [tolerance=±5% resistance=220k package=THT]
  41_-_42 = Rectifier Diode [part_number=1N4001 package="300 mil [THT]"]
  43_-_44 = Rectifier Diode [part_number=1N4001 package="300 mil [THT]"]
  8_OHM = TRANSFORMER [package=transformer]
  +_4_5V_- = Screw terminal - 2 pins [package=THT]
  900CT = female pin header, 1 pin [form="♀ (female)"]
  7476 = IC, DIP package, 16 pins [chip_label=IC]
  SPKR = Screw terminal - 2 pins [package=THT]
  167_-_168 = Pushbutton [package="[THT]"]
  144_com = 7 Segment Display
  820 = Resistor [tolerance=±5% resistance=820 package=THT]
  820_2 = Resistor [tolerance=±5% resistance=820 package=THT]
  820_3 = Resistor [tolerance=±5% resistance=820 package=THT]
  820_4 = Resistor [tolerance=±5% resistance=820 package=THT]
  POWER = Toggle Switch [package=THT]
  50K = Rotary Potentiometer (Small) [maximum_resistance=50kΩ package=THT]
  71_-_72 = Rectifier Diode [part_number=1N4001 package="300 mil [THT]"]
  PNP = PNP-Transistor [package="TO92 [THT]"]
  PNP_2 = PNP-Transistor [package="TO92 [THT]"]
  NPN = NPN-Transistor [package="TO92 [THT]"]
  0_01uF = Ceramic Capacitor [capacitance=10nF package="100 mil [THT, multilayer]"]
  0_1uF = Ceramic Capacitor [capacitance=100nF package="100 mil [THT, multilayer]"]
  3_3uF = Electrolytic Capacitor [capacitance=3.3µF package="100 mil [THT, electrolytic]"]
  100uF = Electrolytic Capacitor [capacitance=100µF package="100 mil [THT, electrolytic]"]
  100uF_2 = Electrolytic Capacitor [capacitance=100µF package="100 mil [THT, electrolytic]"]
  7400 = IC, DIP package, 14 pins [chip_label=IC]
  D2 = Rectifier Diode [part_number=1N4001 package="300 mil [THT]"]
  SOUND = Toggle Switch [package=THT]

nets:
  N1: 330.Pin_0, 7476.pin2, 7476.pin3, 7476.pin4, 7476.pin5, 7476.pin7, 7476.pin8, 7476.pin9, 7476.pin12, 7476.pin16, 167_-_168.Pin_1, 167_-_168.Pin_2, 144_com.common_anode, POWER.COM, PNP_2.E, 7400.pin14
  N2: 330.Pin_1, 470.Pin_0, 7476.pin1, PNP.B, NPN.C
  N3: 470.Pin_1, +_4_5V_-.pin1, 900CT.pin1, 7476.pin13, NPN.E, 3_3uF.-, 100uF.-, 100uF_2.-, 7400.pin7
  N4: 10K.Pin_0, 50K.leg1
  N5: 10K.Pin_1, 167_-_168.Pin_3, 167_-_168.Pin_4, 100uF.+, 100uF_2.+
  N6: 33K.Pin_0, 47K.Pin_0, 100K.Pin_0, 220K.Pin_0, PNP_2.B, 0_01uF.0
  N7: 33K.Pin_1, D2.anode
  N8: 47K.Pin_1, 41_-_42.anode
  N9: 100K.Pin_1, 43_-_44.anode
  N10: 220K.Pin_1, 71_-_72.anode
  N11: 41_-_42.cathode, 820_3.Pin_1, 7400.pin3
  N12: 43_-_44.cathode, 820_2.Pin_0, 7400.pin8
  N13: 8_OHM.1, PNP_2.C, 0_1uF.0
  N14: 8_OHM.2, 0_01uF.1, 0_1uF.1
  N15: 8_OHM.3, SOUND.COM
  N16: 8_OHM.4, SPKR.pin1
  N17: +_4_5V_-.pin2, POWER.L1
  N18: 7476.pin6, 7476.pin15, 7400.pin1, 7400.pin4
  N19: 7476.pin10, 7400.pin2, 7400.pin12
  N20: 7476.pin11, 7400.pin5, 7400.pin9
  N21: 7476.pin14, 7400.pin10, 7400.pin13
  N22: SPKR.pin2, SOUND.L1
  N23: 144_com.Segment_G, 820.Pin_1
  N24: 144_com.Segment_E, 820_2.Pin_1
  N25: 144_com.Segment_D, 820_3.Pin_0
  N26: 144_com.Segment_C, 820_4.Pin_0
  N27: 820.Pin_0, 71_-_72.cathode, 7400.pin6
  N28: 820_4.Pin_1, 7400.pin11, D2.cathode
  N29: 50K.wiper, PNP.E, 3_3uF.+
  N30: PNP.C, NPN.B

notes:
  1/200 WHEEL OF FORTUNE
  g
  com
  e
  d
  c
  Miss Diode Seal of Approval
  github.com/RebeccaRGB/200in1
