# Fritzing sketch 002TheNoisyLight (saved by Fritzing 0.9.3b)
circuit board: 7cm x 3cm
breadboards: 1

parts:
  100 = Resistor [tolerance=±5% resistance=100 package=THT]
  470 = Resistor [tolerance=±5% resistance=470 package=THT]
  4_7K = Resistor [tolerance=±5% resistance=4.7k package=THT]
  4_7K_2 = Resistor [tolerance=±5% resistance=4.7k package=THT]
  PNP = PNP-Transistor [package="TO92 [THT]"]
  PNP_2 = PNP-Transistor [package="TO92 [THT]"]
  152_153 = LED - 5mm [color="Red (633nm)" package="5 mm [THT]"]
  100uF = Electrolytic Capacitor [capacitance=100µF package="100 mil [THT, electrolytic]"]
  100uF_2 = Electrolytic Capacitor [capacitance=100µF package="100 mil [THT, electrolytic]"]
  167_168 = Pushbutton [package="[THT]"]
  SPKR = Screw terminal - 2 pins [package=THT]
  41_42 = Rectifier Diode [part_number=1N4001 package="300 mil [THT]"]
  43_44 = Rectifier Diode [part_number=1N4001 package="300 mil [THT]"]
  +_9V_- = Screw terminal - 2 pins [package=THT]
  8_OHM = TRANSFORMER [package=transformer]

nets:
  N1: 100.Pin_0, 8_OHM.1
  N2: 100.Pin_1, 4_7K.Pin_0, 4_7K_2.Pin_0, 152_153.cathode, +_9V_-.pin1
  N3: 470.Pin_0, 152_153.anode
  N4: 470.Pin_1, PNP.C, 100uF.-
  N5: 4_7K.Pin_1, PNP.B, 100uF_2.+
  N6: 4_7K_2.Pin_1, PNP_2.B, 100uF.+
  N7: PNP.E, 41_42.cathode
  N8: PNP_2.E, 43_44.cathode
  N9: PNP_2.C, 100uF_2.-, 8_OHM.2
  N10: 167_168.Pin_1, 167_168.Pin_2, +_9V_-.pin2
  N11: 167_168.Pin_3, 167_168.Pin_4, 41_42.anode, 43_44.anode
  N12: SPKR.pin1, 8_OHM.4
  N13: SPKR.pin2, 8_OHM.3

notes:
  900
  2/200 THE NOISY LIGHT
  github.com/RebeccaRGB/200in1
  Miss Diode Seal of Approval
