# Fritzing sketch 003ElectronicCandle (saved by Fritzing 0.9.3b)
circuit board: 7cm x 3cm
breadboards: 1

parts:
  470 = Resistor [tolerance=±5% resistance=470 package=THT]
  50K = Rotary Potentiometer (Small) [maximum_resistance=50kΩ package=THT]
  POWER = Toggle Switch [package=THT]
  PNP = PNP-Transistor [package="TO92 [THT]"]
  43_44 = Rectifier Diode [part_number=1N4001 package="300 mil [THT]"]
  169_170 = LED - 5mm [color="Red (633nm)" package="5 mm [THT]"]
  CdS = PHOTOCELL [package=photocell-kit]
  9V_500_OHM = Relay [part_number=FRS1B-S package=THT]
  +_9V_- = Screw terminal - 2 pins [package=THT]

nets:
  N1: 470.Pin_0, 9V_500_OHM.C1, 9V_500_OHM.C2
  N2: 470.Pin_1, 169_170.anode
  N3: 50K.leg1, CdS.P$2
  N4: 50K.wiper, PNP.B
  N5: 50K.leg2, POWER.COM, PNP.E, 9V_500_OHM.B
  N6: POWER.L1, +_9V_-.pin2
  N7: PNP.C, 43_44.cathode, 9V_500_OHM.COIL1
  N8: 43_44.anode, 169_170.cathode, CdS.P$1, 9V_500_OHM.COIL2, +_9V_-.pin1

notes:
  3/200 ELECTRONIC CANDLE
  github.com/RebeccaRGB/200in1
  Miss Diode Seal of Approval
