# Fritzing sketch 004RainDetector (saved by Fritzing 0.9.3b)
circuit board: 3cm x 3cm
breadboards: 1

parts:
  POWER = Toggle Switch [package=THT]
  2_2K = Resistor [tolerance=±5% resistance=2.2k package=THT]
  4_7K = Resistor [tolerance=±5% resistance=4.7k package=THT]
  PNP = PNP-Transistor [package="TO92 [THT]"]
  0_01uF = Ceramic Capacitor [capacitance=10nF package="100 mil [THT, multilayer]"]
  0_1uF = Ceramic Capacitor [capacitance=100nF package="100 mil [THT, multilayer]"]
  SPKR = Screw terminal - 2 pins [package=THT]
  LEADS = Screw terminal - 2 pins [package=THT]
  +4_5V- = Screw terminal - 2 pins [package=THT]
  8_OHM = TRANSFORMER [package=transformer]
  900CT = female pin header, 1 pin [form="♀ (female)"]

nets:
  N1: POWER.L1, +4_5V-.pin2
  N2: POWER.COM, 2_2K.Pin_1, PNP.E
  N3: 2_2K.Pin_0, 4_7K.Pin_0, PNP.B, 0_01uF.0
  N4: 4_7K.Pin_1, LEADS.pin1
  N5: PNP.C, 0_1uF.0, 8_OHM.2
  N6: 0_01uF.1, 0_1uF.1, 8_OHM.1
  N7: SPKR.pin1, 8_OHM.4
  N8: SPKR.pin2, 8_OHM.3
  N9: LEADS.pin2, +4_5V-.pin1, 900CT.pin1

notes:
  4/200 RAIN DETECTOR
  github.com/RebeccaRGB/200in1
  Miss Diode
  Seal of Approval
