# Fritzing sketch 005EarSplitter (saved by Fritzing 0.9.3b)
circuit board: 3cm x 3cm
breadboards: 1

parts:
  POWER = Toggle Switch [package=THT]
  47K = Resistor [tolerance=±5% resistance=47k package=THT]
  PNP = PNP-Transistor [package="TO92 [THT]"]
  0_01uF = Ceramic Capacitor [capacitance=10nF package="100 mil [THT, multilayer]"]
  0_05uF = Ceramic Capacitor [capacitance=50nF package="100 mil [THT, multilayer]"]
  0_1uF = Ceramic Capacitor [capacitance=100nF package="100 mil [THT, multilayer]"]
  167_168 = Pushbutton [package="[THT]"]
  SPKR = Screw terminal - 2 pins [package=THT]
  +4_5V- = Screw terminal - 2 pins [package=THT]
  8_OHM = TRANSFORMER [package=transformer]
  900CT = female pin header, 1 pin [form="♀ (female)"]

nets:
  N1: POWER.L1, +4_5V-.pin2
  N2: POWER.COM, PNP.E
  N3: 47K.Pin_0, PNP.B, 0_05uF.0, 167_168.Pin_1, 167_168.Pin_2
  N4: 47K.Pin_1, +4_5V-.pin1, 900CT.pin1
  N5: PNP.C, 0_1uF.0, 8_OHM.2
  N6: 0_01uF.0, 167_168.Pin_3, 167_168.Pin_4
  N7: 0_01uF.1, 0_05uF.1, 0_1uF.1, 8_OHM.1
  N8: SPKR.pin1, 8_OHM.4
  N9: SPKR.pin2, 8_OHM.3

notes:
  5/200 EAR SPLITTER
  Seal of Approval
  github.com/RebeccaRGB/200in1
  Miss Diode
