# Fritzing sketch 006PencilLeadOrgan (saved by Fritzing 0.9.3b)
circuit board: 3cm x 3cm
breadboards: 1

parts:
  8_OHM = TRANSFORMER [package=transformer]
  900CT = female pin header, 1 pin [form="♀ (female)"]
  4_7K = Resistor [tolerance=±5% resistance=4.7k package=THT]
  22K = Resistor [tolerance=±5% resistance=22k package=THT]
  +4_5V- = Screw terminal - 2 pins [package=THT]
  NPN = NPN-Transistor [package="TO92 [THT]"]
  0_05uF = Ceramic Capacitor [capacitance=50nF package="100 mil [THT, multilayer]"]
  0_1uF = Ceramic Capacitor [capacitance=100nF package="100 mil [THT, multilayer]"]
  POWER = Toggle Switch [package=THT]
  SPKR = Screw terminal - 2 pins [package=THT]
  LEADS = Screw terminal - 2 pins [package=THT]

nets:
  N1: 8_OHM.1, 0_05uF.0, 0_1uF.0
  N2: 8_OHM.2, NPN.C, 0_1uF.1
  N3: 8_OHM.3, SPKR.pin2
  N4: 8_OHM.4, SPKR.pin1
  N5: 900CT.pin1, 4_7K.Pin_1, POWER.COM
  N6: 4_7K.Pin_0, LEADS.pin2
  N7: 22K.Pin_0, +4_5V-.pin1, NPN.E
  N8: 22K.Pin_1, NPN.B, 0_05uF.1, LEADS.pin1
  N9: +4_5V-.pin2, POWER.L1

notes:
  6/200 PENCIL LEAD ORGAN
  Seal of Approval
  github.com/RebeccaRGB/200in1
  Miss Diode
