# Fritzing sketch 007TheElectricHuman (saved by Fritzing 0.9.3b)
circuit board: 3cm x 3cm
breadboards: 1

parts:
  470 = Resistor [tolerance=±5% resistance=470 package=THT]
  1K = Resistor [tolerance=±5% resistance=1k package=THT]
  4_7K = Resistor [tolerance=±5% resistance=4.7k package=THT]
  10K = Resistor [tolerance=±5% resistance=10k package=THT]
  100K = Resistor [tolerance=±5% resistance=100k package=THT]
  +9V- = Screw terminal - 2 pins [package=THT]
  NPN = NPN-Transistor [package="TO92 [THT]"]
  PNP = PNP-Transistor [package="TO92 [THT]"]
  50K = Rotary Potentiometer (Small) [maximum_resistance=50kΩ package=THT]
  POWER = Toggle Switch [package=THT]
  +METER- = Screw terminal - 2 pins [package=THT]
  LEADS = Screw terminal - 2 pins [package=THT]

nets:
  N1: 470.Pin_0, 1K.Pin_0, POWER.COM, LEADS.pin2
  N2: 470.Pin_1, PNP.E
  N3: 1K.Pin_1, NPN.C, PNP.B
  N4: 4_7K.Pin_0, 50K.wiper
  N5: 4_7K.Pin_1, 100K.Pin_0, LEADS.pin1
  N6: 10K.Pin_0, +METER-.pin2
  N7: 10K.Pin_1, PNP.C
  N8: 100K.Pin_1, NPN.B
  N9: +9V-.pin1, NPN.E, 50K.leg2, +METER-.pin1
  N10: +9V-.pin2, POWER.L1

notes:
  7/200 THE ELECTRIC HUMAN
  Seal of Approval
  github.com/RebeccaRGB/200in1
  Miss Diode
