# Fritzing sketch 008TheElectrosonicHuman (saved by Fritzing 0.9.3b)
circuit board: 7cm x 3cm
breadboards: 1

parts:
  8_OHM = TRANSFORMER [package=transformer]
  900CT = female pin header, 1 pin [form="♀ (female)"]
  4_7K = Resistor [tolerance=±5% resistance=4.7k package=THT]
  +4_5V- = Screw terminal - 2 pins [package=THT]
  PNP = PNP-Transistor [package="TO92 [THT]"]
  0_01uF = Ceramic Capacitor [capacitance=10nF package="100 mil [THT, multilayer]"]
  0_1uF = Ceramic Capacitor [capacitance=100nF package="100 mil [THT, multilayer]"]
  50K = Rotary Potentiometer (Small) [maximum_resistance=50kΩ package=THT]
  POWER = Toggle Switch [package=THT]
  LEADS = Screw terminal - 2 pins [package=THT]
  SPKR = Screw terminal - 2 pins [package=THT]

nets:
  N1: 8_OHM.1, 0_01uF.1, 0_1uF.1
  N2: 8_OHM.2, PNP.C, 0_1uF.0
  N3: 8_OHM.3, SPKR.pin2
  N4: 8_OHM.4, SPKR.pin1
  N5: 900CT.pin1, +4_5V-.pin1, 50K.wiper
  N6: 4_7K.Pin_0, LEADS.pin1
  N7: 4_7K.Pin_1, PNP.B, 0_01uF.0
  N8: +4_5V-.pin2, POWER.L1
  N9: PNP.E, POWER.COM
  N10: 50K.leg1, LEADS.pin2

notes:
  8/200 THE ELECTROSONIC HUMAN
  github.com/RebeccaRGB/200in1
  Miss Diode Seal of Approval
