# Fritzing sketch 009ElectricBirthdayCake (saved by Fritzing 0.9.3b)
circuit board: 7cm x 3cm
breadboards: 1

parts:
  330 = Resistor [tolerance=±5% resistance=330 package=THT]
  330_2 = Resistor [tolerance=±5% resistance=330 package=THT]
  470 = Resistor [tolerance=±5% resistance=470 package=THT]
  470_2 = Resistor [tolerance=±5% resistance=470 package=THT]
  470_3 = Resistor [tolerance=±5% resistance=470 package=THT]
  470_4 = Resistor [tolerance=±5% resistance=470 package=THT]
  100K = Resistor [tolerance=±5% resistance=100k package=THT]
  43_44#1 = Rectifier Diode [part_number=1N4001 package="300 mil [THT]"]
  +4_5V- = Screw terminal - 2 pins [package=THT]
  7400 = IC, DIP package, 14 pins [chip_label=IC]
  NPN = NPN-Transistor [package="TO92 [THT]"]
  NPN_2 = NPN-Transistor [package="TO92 [THT]"]
  PNP = PNP-Transistor [package="TO92 [THT]"]
  PNP_2 = PNP-Transistor [package="TO92 [THT]"]
  100uF = Electrolytic Capacitor [capacitance=100µF package="100 mil [THT, electrolytic]"]
  50K = Rotary Potentiometer (Small) [maximum_resistance=50kΩ package=THT]
  POWER = Toggle Switch [package=THT]
  156_157#1 = LED - 5mm [color="Red (633nm)" package="5 mm [THT]"]
  154_155#1 = LED - 5mm [color="Red (633nm)" package="5 mm [THT]"]
  152_153#1 = LED - 5mm [color="Red (633nm)" package="5 mm [THT]"]
  EAR = Screw terminal - 2 pins [package=THT]

nets:
  N1: 330.Pin_0, 330_2.Pin_0, 470.Pin_0, 470_2.Pin_0, 470_3.Pin_0, 470_4.Pin_0, 100K.Pin_1, +4_5V-.pin1, 7400.pin7, 7400.pin9, 7400.pin10, 100uF.-
  N2: 330.Pin_1, 7400.pin1, NPN_2.E
  N3: 330_2.Pin_1, 7400.pin13, NPN.B, NPN_2.B, PNP.C, PNP_2.C, 100uF.+
  N4: 470.Pin_1, 156_157#1.cathode
  N5: 470_2.Pin_1, 154_155#1.cathode
  N6: 470_3.Pin_1, 43_44#1.cathode, 7400.pin4
  N7: 470_4.Pin_1, 152_153#1.cathode
  N8: 100K.Pin_0, 50K.leg1, EAR.pin1
  N9: 43_44#1.anode, NPN.E
  N10: +4_5V-.pin2, POWER.L1
  N11: 7400.pin2, 7400.pin5, 7400.pin12, 7400.pin14, NPN.C, NPN_2.C, PNP.E, 50K.leg2, POWER.COM, EAR.pin2
  N12: 7400.pin3, 154_155#1.anode
  N13: 7400.pin6, 156_157#1.anode
  N14: 7400.pin11, 152_153#1.anode
  N15: PNP.B, PNP_2.E
  N16: PNP_2.B, 50K.wiper

notes:
  9/200 ELECTRIC BIRTHDAY CAKE
  github.com/RebeccaRGB/200in1
  Miss Diode Seal of Approval
