# Fritzing sketch 010QuickDraw (saved by Fritzing 0.9.3b)
circuit board: 7cm x 3cm
breadboards: 1

parts:
  330 = Resistor [tolerance=±5% resistance=330 package=THT]
  330_2 = Resistor [tolerance=±5% resistance=330 package=THT]
  470 = Resistor [tolerance=±5% resistance=470 package=THT]
  470_2 = Resistor [tolerance=±5% resistance=470 package=THT]
  10K = Resistor [tolerance=±5% resistance=10k package=THT]
  +_4_5V_- = Screw terminal - 2 pins [package=THT]
  7476 = IC, DIP package, 16 pins [chip_label=IC]
  POWER = Toggle Switch [package=THT]
  P2 = LED - 5mm [color="Red (633nm)" package="5 mm [THT]"]
  P1 = LED - 5mm [color="Red (633nm)" package="5 mm [THT]"]
  167_168#1 = Pushbutton [package="[THT]"]
  P2_2 = Screw terminal - 2 pins [package=THT]
  P1_2 = Screw terminal - 2 pins [package=THT]

nets:
  N1: 330.Pin_0, 7476.pin6, P2_2.pin1
  N2: 330.Pin_1, 330_2.Pin_1, +_4_5V_-.pin1, 7476.pin12, 7476.pin13, 7476.pin16, 167_168#1.Pin_3, 167_168#1.Pin_4
  N3: 330_2.Pin_0, 7476.pin1, P1_2.pin2
  N4: 470.Pin_0, 470_2.Pin_0, 10K.Pin_0, 7476.pin2, 7476.pin5, 7476.pin7, POWER.COM, P2_2.pin2, P1_2.pin1
  N5: 470.Pin_1, P2.anode
  N6: 470_2.Pin_1, P1.anode
  N7: 10K.Pin_1, 7476.pin3, 7476.pin8, 167_168#1.Pin_1, 167_168#1.Pin_2
  N8: +_4_5V_-.pin2, POWER.L1
  N9: 7476.pin4, 7476.pin10, P2.cathode
  N10: 7476.pin9, 7476.pin14, P1.cathode

notes:
  10/200 QUICK DRAW
  github.com/RebeccaRGB/200in1
  Miss Diode Seal of Approval
