# Fritzing sketch 011QuickDrawII (saved by Fritzing 0.9.3b)
circuit board: 7cm x 7cm
breadboards: 1

parts:
  330 = Resistor [tolerance=±5% resistance=330 package=THT]
  330_2 = Resistor [tolerance=±5% resistance=330 package=THT]
  470 = Resistor [tolerance=±5% resistance=470 package=THT]
  470_2 = Resistor [tolerance=±5% resistance=470 package=THT]
  470_3 = Resistor [tolerance=±5% resistance=470 package=THT]
  1K = Resistor [tolerance=±5% resistance=1k package=THT]
  1K_2 = Resistor [tolerance=±5% resistance=1k package=THT]
  10K = Resistor [tolerance=±5% resistance=10k package=THT]
  33K = Resistor [tolerance=±5% resistance=33k package=THT]
  43_44#1 = Rectifier Diode [part_number=1N4001 package="300 mil [THT]"]
  7400 = IC, DIP package, 14 pins [chip_label=IC]
  7476 = IC, DIP package, 16 pins [chip_label=IC]
  NPN = NPN-Transistor [package="TO92 [THT]"]
  NPN_2 = NPN-Transistor [package="TO92 [THT]"]
  100uF = Electrolytic Capacitor [capacitance=100µF package="100 mil [THT, electrolytic]"]
  POWER = Toggle Switch [package=THT]
  144_com2 = 7 Segment Display
  820 = Resistor [tolerance=±5% resistance=820 package=THT]
  820_2 = Resistor [tolerance=±5% resistance=820 package=THT]
  820_3 = Resistor [tolerance=±5% resistance=820 package=THT]
  820_4 = Resistor [tolerance=±5% resistance=820 package=THT]
  162_163#1 = LED - 5mm [color="Red (633nm)" package="5 mm [THT]"]
  160_161#1 = LED - 5mm [color="Red (633nm)" package="5 mm [THT]"]
  158_159#1 = LED - 5mm [color="Red (633nm)" package="5 mm [THT]"]
  156_157#1 = LED - 5mm [color="Red (633nm)" package="5 mm [THT]"]
  154_155#1 = LED - 5mm [color="Red (633nm)" package="5 mm [THT]"]
  167_168#1 = Pushbutton [package="[THT]"]
  P2 = Screw terminal - 2 pins [package=THT]
  P1 = Screw terminal - 2 pins [package=THT]
  +_4_5V_- = Screw terminal - 2 pins [package=THT]

nets:
  N1: 330.Pin_0, 7476.pin6, P2.pin1
  N2: 330.Pin_1, 330_2.Pin_1, 7400.pin7, 7476.pin9, 7476.pin13, 7476.pin16, NPN.E, NPN_2.E, 167_168#1.Pin_3, 167_168#1.Pin_4, +_4_5V_-.pin1
  N3: 330_2.Pin_0, 7476.pin1, P1.pin2
  N4: 470.Pin_0, 470_2.Pin_1, 1K.Pin_0, 1K_2.Pin_0, 33K.Pin_0, 7400.pin14, 7476.pin2, 7476.pin5, 7476.pin8, POWER.COM, 144_com2.common_anode, 158_159#1.anode, P2.pin2, P1.pin1
  N5: 470.Pin_1, 162_163#1.anode, 160_161#1.anode
  N6: 470_2.Pin_0, 156_157#1.anode, 154_155#1.anode
  N7: 470_3.Pin_0, 158_159#1.cathode
  N8: 470_3.Pin_1, 10K.Pin_0, 7400.pin13, NPN.C
  N9: 1K.Pin_1, 43_44#1.cathode, 7400.pin4, 7476.pin3, 7476.pin7, 167_168#1.Pin_1, 167_168#1.Pin_2
  N10: 1K_2.Pin_1, 43_44#1.anode, NPN_2.C, 100uF.+
  N11: 10K.Pin_1, NPN_2.B
  N12: 33K.Pin_1, NPN.B, 100uF.-
  N13: 7400.pin1, 7476.pin12, 7476.pin14, 154_155#1.cathode
  N14: 7400.pin2, 7476.pin4, 7476.pin11, 162_163#1.cathode
  N15: 7400.pin3, 7400.pin12
  N16: 7400.pin5, 7400.pin8
  N17: 7400.pin6, 7400.pin9, 820.Pin_0, 820_2.Pin_0, 820_3.Pin_0, 820_4.Pin_0
  N18: 7400.pin10, 7400.pin11
  N19: 7476.pin10, 160_161#1.cathode
  N20: 7476.pin15, 156_157#1.cathode
  N21: POWER.L1, +_4_5V_-.pin2
  N22: 144_com2.Segment_G, 820.Pin_1
  N23: 144_com2.Segment_F, 820_2.Pin_1
  N24: 144_com2.Segment_E, 820_3.Pin_1
  N25: 144_com2.Segment_A, 820_4.Pin_1

notes:
  com
  e
  a
  f
  g
  github.com/RebeccaRGB/200in1
  Miss Diode Seal of Approval
  11/200 QUICK DRAW II
