# Fritzing sketch 012ElectronicSafecracking (saved by Fritzing 0.9.3b)
circuit board: 7cm x 3cm
breadboards: 1

parts:
  470 = Resistor [tolerance=±5% resistance=470 package=THT]
  2K = TRANSFORMER [package=transformer]
  4K_CT = female pin header, 1 pin [form="♀ (female)"]
  33K = Resistor [tolerance=±5% resistance=33k package=THT]
  71_72#1 = Rectifier Diode [part_number=1N4001 package="300 mil [THT]"]
  43_44#1 = Rectifier Diode [part_number=1N4001 package="300 mil [THT]"]
  41_42#1 = Rectifier Diode [part_number=1N4001 package="300 mil [THT]"]
  +_9V_- = Screw terminal - 2 pins [package=THT]
  NPN = NPN-Transistor [package="TO92 [THT]"]
  0_005uF = Ceramic Capacitor [capacitance=5nF package="100 mil [THT, multilayer]"]
  0_01uF = Ceramic Capacitor [capacitance=10nF package="100 mil [THT, multilayer]"]
  0_05uF = Ceramic Capacitor [capacitance=50nF package="100 mil [THT, multilayer]"]
  0_1uF = Ceramic Capacitor [capacitance=100nF package="100 mil [THT, multilayer]"]
  50K = Rotary Potentiometer (Small) [maximum_resistance=50kΩ package=THT]
  SOUND = Toggle Switch [package=THT]
  167_168#1 = Pushbutton [package="[THT]"]
  EAR = Screw terminal - 2 pins [package=THT]

nets:
  N1: 470.Pin_0, 50K.wiper, SOUND.COM
  N2: 470.Pin_1, 43_44#1.anode, 41_42#1.cathode, EAR.pin1
  N3: 2K.1, 0_05uF.0, 0_1uF.0
  N4: 2K.2, NPN.C, 0_1uF.1
  N5: 2K.3, 0_01uF.1, 50K.leg2
  N6: 2K.4, 0_005uF.1, 50K.leg1
  N7: 4K_CT.pin1, 33K.Pin_1, 167_168#1.Pin_3, 167_168#1.Pin_4
  N8: 33K.Pin_0, 71_72#1.cathode, NPN.B, 0_05uF.1
  N9: 71_72#1.anode, +_9V_-.pin1, NPN.E
  N10: 43_44#1.cathode, 41_42#1.anode, 0_005uF.0, 0_01uF.0
  N11: +_9V_-.pin2, 167_168#1.Pin_1, 167_168#1.Pin_2
  N12: SOUND.L1, EAR.pin2

notes:
  12/200 ELECTRONIC SAFECRACKING
  github.com/RebeccaRGB/200in1
  Miss Diode Seal of Approval
