# Fritzing sketch 013UFOInvasion (saved by Fritzing 0.9.3b)
circuit board: 7cm x 7cm
breadboards: 1

parts:
  100 = Resistor [tolerance=±5% resistance=100 package=THT]
  470 = Resistor [tolerance=±5% resistance=470 package=THT]
  1K = Resistor [tolerance=±5% resistance=1k package=THT]
  1K_2 = Resistor [tolerance=±5% resistance=1k package=THT]
  8_OHM = TRANSFORMER [package=transformer]
  900CT = female pin header, 1 pin [form="♀ (female)"]
  4_7K = Resistor [tolerance=±5% resistance=4.7k package=THT]
  4_7K_2 = Resistor [tolerance=±5% resistance=4.7k package=THT]
  10K = Resistor [tolerance=±5% resistance=10k package=THT]
  22K = Resistor [tolerance=±5% resistance=22k package=THT]
  33K = Resistor [tolerance=±5% resistance=33k package=THT]
  100K = Resistor [tolerance=±5% resistance=100k package=THT]
  71_72#1 = Rectifier Diode [part_number=1N4001 package="300 mil [THT]"]
  43_44#1 = Rectifier Diode [part_number=1N4001 package="300 mil [THT]"]
  41_42#1 = Rectifier Diode [part_number=1N4001 package="300 mil [THT]"]
  +_4_5V_- = Screw terminal - 2 pins [package=THT]
  7400 = IC, DIP package, 14 pins [chip_label=IC]
  7476 = IC, DIP package, 16 pins [chip_label=IC]
  NPN = NPN-Transistor [package="TO92 [THT]"]
  NPN_2 = NPN-Transistor [package="TO92 [THT]"]
  PNP = PNP-Transistor [package="TO92 [THT]"]
  PNP_2 = PNP-Transistor [package="TO92 [THT]"]
  0_05uF = Ceramic Capacitor [capacitance=50nF package="100 mil [THT, multilayer]"]
  0_1uF = Ceramic Capacitor [capacitance=100nF package="100 mil [THT, multilayer]"]
  100uF = Electrolytic Capacitor [capacitance=100µF package="100 mil [THT, electrolytic]"]
  100uF_2 = Electrolytic Capacitor [capacitance=100µF package="100 mil [THT, electrolytic]"]
  10uF = Electrolytic Capacitor [capacitance=10µF package="100 mil [THT, electrolytic]"]
  3_3uF = Electrolytic Capacitor [capacitance=3.3µF package="100 mil [THT, electrolytic]"]
  50K = Rotary Potentiometer (Small) [maximum_resistance=50kΩ package=THT]
  POWER = Toggle Switch [package=THT]
  144_com2 = 7 Segment Display
  820 = Resistor [tolerance=±5% resistance=820 package=THT]
  820_2 = Resistor [tolerance=±5% resistance=820 package=THT]
  820_3 = Resistor [tolerance=±5% resistance=820 package=THT]
  820_4 = Resistor [tolerance=±5% resistance=820 package=THT]
  820_5 = Resistor [tolerance=±5% resistance=820 package=THT]
  820_6 = Resistor [tolerance=±5% resistance=820 package=THT]
  820_7 = Resistor [tolerance=±5% resistance=820 package=THT]
  152_153#1 = LED - 5mm [color="Red (633nm)" package="5 mm [THT]"]
  167_168#1 = Pushbutton [package="[THT]"]
  SPKR = Screw terminal - 2 pins [package=THT]
  SOUND = Toggle Switch [package=THT]

nets:
  N1: 100.Pin_0, 1K.Pin_0, +_4_5V_-.pin1, 7400.pin7, 7476.pin13, NPN.E, NPN_2.E, 100uF.-, 100uF_2.-, 10uF.-, 3_3uF.-
  N2: 100.Pin_1, 7400.pin2, 167_168#1.Pin_3, 167_168#1.Pin_4
  N3: 470.Pin_0, 1K_2.Pin_0, 4_7K_2.Pin_0, 10K.Pin_0, 22K.Pin_0, 7400.pin14, 7476.pin2, 7476.pin3, 7476.pin4, 7476.pin5, 7476.pin7, 7476.pin8, 7476.pin9, 7476.pin12, 7476.pin16, PNP_2.E, POWER.COM, 144_com2.common_anode
  N4: 470.Pin_1, 152_153#1.anode
  N5: 1K.Pin_1, 1K_2.Pin_1, 41_42#1.cathode, 7476.pin1, NPN_2.C, PNP.B
  N6: 8_OHM.1, 0_05uF.0, 0_1uF.0
  N7: 8_OHM.2, NPN.C, 0_1uF.1
  N8: 8_OHM.3, SOUND.COM
  N9: 8_OHM.4, SPKR.pin1
  N10: 900CT.pin1, 100K.Pin_0, PNP_2.C
  N11: 4_7K.Pin_0, 50K.leg1
  N12: 4_7K.Pin_1, 10K.Pin_1, 43_44#1.anode, 100uF_2.+
  N13: 4_7K_2.Pin_1, 100uF.+, 167_168#1.Pin_1, 167_168#1.Pin_2
  N14: 22K.Pin_1, 33K.Pin_0, 41_42#1.anode, 10uF.+
  N15: 33K.Pin_1, PNP_2.B
  N16: 100K.Pin_1, NPN.B, 0_05uF.1
  N17: 71_72#1.cathode, 43_44#1.cathode, 7400.pin3
  N18: 71_72#1.anode, PNP.E, 3_3uF.+, 50K.wiper
  N19: +_4_5V_-.pin2, POWER.L1
  N20: 7400.pin1, 7400.pin8, 820_2.Pin_0, 820_3.Pin_0
  N21: 7400.pin4, 7400.pin13, 7476.pin14, 820_4.Pin_1, 820_5.Pin_1, 820_6.Pin_1
  N22: 7400.pin5, 7476.pin11
  N23: 7400.pin6, 820.Pin_0
  N24: 7400.pin9, 7400.pin10, 7400.pin11, 152_153#1.cathode
  N25: 7400.pin12, 7476.pin10, 820_7.Pin_1
  N26: 7476.pin6, 7476.pin15
  N27: NPN_2.B, PNP.C
  N28: 144_com2.Segment_G, 820.Pin_1
  N29: 144_com2.Segment_F, 820_2.Pin_1
  N30: 144_com2.Segment_E, 820_3.Pin_1
  N31: 144_com2.Segment_D, 820_4.Pin_0
  N32: 144_com2.Segment_C, 820_5.Pin_0
  N33: 144_com2.Segment_B, 820_6.Pin_0
  N34: 144_com2.Segment_A, 820_7.Pin_0
  N35: SPKR.pin2, SOUND.L1

notes:
  c
  com
  e
  d
  a
  b
  f
  g
  github.com/RebeccaRGB/200in1
  Miss Diode Seal of Approval
  13/200 UFO INVASION
  >
