# Fritzing sketch 014TugOfWar (saved by Fritzing 0.9.3b)
circuit board: 7cm x 3cm
breadboards: 1

parts:
  330 = Resistor [tolerance=±5% resistance=330 package=THT]
  330_2 = Resistor [tolerance=±5% resistance=330 package=THT]
  1K = Resistor [tolerance=±5% resistance=1k package=THT]
  1K_2 = Resistor [tolerance=±5% resistance=1k package=THT]
  10K = Resistor [tolerance=±5% resistance=10k package=THT]
  33K = Resistor [tolerance=±5% resistance=33k package=THT]
  100K = Resistor [tolerance=±5% resistance=100k package=THT]
  +9V- = Screw terminal - 2 pins [package=THT]
  NPN = NPN-Transistor [package="TO92 [THT]"]
  NPN_2 = NPN-Transistor [package="TO92 [THT]"]
  PNP = PNP-Transistor [package="TO92 [THT]"]
  PNP_2 = PNP-Transistor [package="TO92 [THT]"]
  50K = Rotary Potentiometer (Small) [maximum_resistance=50kΩ package=THT]
  POWER = Toggle Switch [package=THT]
  +METER- = Screw terminal - 2 pins [package=THT]
  P1 = Screw terminal - 2 pins [package=THT]
  P2 = Screw terminal - 2 pins [package=THT]

nets:
  N1: 330.Pin_0, 330_2.Pin_0, +METER-.pin2
  N2: 330.Pin_1, NPN.E
  N3: 330_2.Pin_1, PNP.E
  N4: 1K.Pin_0, 10K.Pin_0, NPN.C, NPN_2.C, POWER.COM, P1.pin1
  N5: 1K.Pin_1, 1K_2.Pin_1, +METER-.pin1
  N6: 1K_2.Pin_0, 33K.Pin_0, +9V-.pin1, PNP.C, PNP_2.C, P2.pin1
  N7: 10K.Pin_1, 50K.leg1
  N8: 33K.Pin_1, 100K.Pin_1, PNP_2.B, P1.pin2
  N9: 100K.Pin_0, NPN_2.B, 50K.wiper, P2.pin2
  N10: +9V-.pin2, POWER.L1
  N11: NPN.B, NPN_2.E
  N12: PNP.B, PNP_2.E

notes:
  14/200 TUG OF WAR
  Miss Diode Seal of Approval
  github.com/RebeccaRGB/200in1
