# Fritzing sketch 015ShotInTheDark (saved by Fritzing 0.9.3b)
circuit board: 7cm x 3cm
breadboards: 1

parts:
  1K = Resistor [tolerance=±5% resistance=1k package=THT]
  9V_500_OHM = Relay [part_number=FRS1B-S package=THT]
  1K_2 = Resistor [tolerance=±5% resistance=1k package=THT]
  CdS = PHOTOCELL [package=photocell-kit]
  4_7K = Resistor [tolerance=±5% resistance=4.7k package=THT]
  4_7K_2 = Resistor [tolerance=±5% resistance=4.7k package=THT]
  10K = Resistor [tolerance=±5% resistance=10k package=THT]
  220K = Resistor [tolerance=±5% resistance=220k package=THT]
  43_44#1 = Rectifier Diode [part_number=1N4001 package="300 mil [THT]"]
  +_9V_- = Screw terminal - 2 pins [package=THT]
  NPN = NPN-Transistor [package="TO92 [THT]"]
  PNP = PNP-Transistor [package="TO92 [THT]"]
  PNP_2 = PNP-Transistor [package="TO92 [THT]"]
  100uF = Electrolytic Capacitor [capacitance=100µF package="100 mil [THT, electrolytic]"]
  50K = Rotary Potentiometer (Small) [maximum_resistance=50kΩ package=THT]
  POWER = Toggle Switch [package=THT]
  169_170#1 = LED - 5mm [color="Red (633nm)" package="5 mm [THT]"]

nets:
  N1: 1K.Pin_0, 9V_500_OHM.C1, 9V_500_OHM.C2
  N2: 1K.Pin_1, 169_170#1.cathode
  N3: 9V_500_OHM.COIL1, 9V_500_OHM.B, 1K_2.Pin_1, 4_7K.Pin_1, 43_44#1.anode, +_9V_-.pin1, NPN.E, 50K.leg1
  N4: 9V_500_OHM.COIL2, 43_44#1.cathode, PNP.C, 100uF.-
  N5: 1K_2.Pin_0, 4_7K_2.Pin_0, PNP_2.C
  N6: CdS.P$1, 50K.leg2
  N7: CdS.P$2, PNP.E, PNP_2.E, POWER.COM, 169_170#1.anode
  N8: 4_7K.Pin_0, PNP_2.B, 100uF.+
  N9: 4_7K_2.Pin_1, 10K.Pin_1, PNP.B
  N10: 10K.Pin_0, NPN.C
  N11: 220K.Pin_0, 50K.wiper
  N12: 220K.Pin_1, NPN.B
  N13: +_9V_-.pin2, POWER.L1

notes:
  github.com/RebeccaRGB/200in1
  Miss Diode Seal of Approval
  15/200 SHOT IN THE DARK
