# Fritzing sketch 016BurglarAlarm (saved by Fritzing 0.9.3b)
circuit board: 3cm x 3cm
breadboards: 1

parts:
  8_OHM = TRANSFORMER [package=transformer]
  900CT = female pin header, 1 pin [form="♀ (female)"]
  47K = Resistor [tolerance=±5% resistance=47k package=THT]
  +4_5V- = Screw terminal - 2 pins [package=THT]
  NPN = NPN-Transistor [package="TO92 [THT]"]
  0_05uF = Ceramic Capacitor [capacitance=50nF package="100 mil [THT, multilayer]"]
  0_1uF = Ceramic Capacitor [capacitance=100nF package="100 mil [THT, multilayer]"]
  POWER = Toggle Switch [package=THT]
  LOOP = Screw terminal - 2 pins [package=THT]
  SPKR = Screw terminal - 2 pins [package=THT]

nets:
  N1: 8_OHM.1, 0_05uF.0, 0_1uF.0
  N2: 8_OHM.2, NPN.C, 0_1uF.1
  N3: 8_OHM.3, SPKR.pin2
  N4: 8_OHM.4, SPKR.pin1
  N5: 900CT.pin1, 47K.Pin_1, POWER.COM
  N6: 47K.Pin_0, NPN.B, 0_05uF.1, LOOP.pin2
  N7: +4_5V-.pin1, NPN.E, LOOP.pin1
  N8: +4_5V-.pin2, POWER.L1

notes:
  Seal of Approval
  github.com/RebeccaRGB/200in1
  Miss Diode
  16/200 BURGLAR ALARM
