# Fritzing sketch 017SOSAlert (saved by Fritzing 0.9.3b)
circuit board: 7cm x 7cm
breadboards: 1

parts:
  470 = Resistor [tolerance=±5% resistance=470 package=THT]
  470_2 = Resistor [tolerance=±5% resistance=470 package=THT]
  8_OHM = TRANSFORMER [package=transformer]
  900CT = female pin header, 1 pin [form="♀ (female)"]
  4_7K = Resistor [tolerance=±5% resistance=4.7k package=THT]
  4_7K_2 = Resistor [tolerance=±5% resistance=4.7k package=THT]
  47K = Resistor [tolerance=±5% resistance=47k package=THT]
  +_4_5V_- = Screw terminal - 2 pins [package=THT]
  7400 = IC, DIP package, 14 pins [chip_label=IC]
  7476 = IC, DIP package, 16 pins [chip_label=IC]
  NPN = NPN-Transistor [package="TO92 [THT]"]
  NPN_2 = NPN-Transistor [package="TO92 [THT]"]
  PNP = PNP-Transistor [package="TO92 [THT]"]
  0_01uF = Ceramic Capacitor [capacitance=10nF package="100 mil [THT, multilayer]"]
  0_05uF = Ceramic Capacitor [capacitance=50nF package="100 mil [THT, multilayer]"]
  100uF = Electrolytic Capacitor [capacitance=100µF package="100 mil [THT, electrolytic]"]
  100uF_2 = Electrolytic Capacitor [capacitance=100µF package="100 mil [THT, electrolytic]"]
  POWER = Toggle Switch [package=THT]
  144_com2 = 7 Segment Display
  820 = Resistor [tolerance=±5% resistance=820 package=THT]
  820_2 = Resistor [tolerance=±5% resistance=820 package=THT]
  820_3 = Resistor [tolerance=±5% resistance=820 package=THT]
  820_4 = Resistor [tolerance=±5% resistance=820 package=THT]
  820_5 = Resistor [tolerance=±5% resistance=820 package=THT]
  820_6 = Resistor [tolerance=±5% resistance=820 package=THT]
  820_7 = Resistor [tolerance=±5% resistance=820 package=THT]
  162_163#1 = LED - 5mm [color="Red (633nm)" package="5 mm [THT]"]
  160_161#1 = LED - 5mm [color="Red (633nm)" package="5 mm [THT]"]
  SPKR = Screw terminal - 2 pins [package=THT]
  SOUND = Toggle Switch [package=THT]

nets:
  N1: 470.Pin_0, 162_163#1.cathode
  N2: 470.Pin_1, 7400.pin12, 7400.pin13, NPN.C, 100uF.+
  N3: 470_2.Pin_0, 160_161#1.cathode
  N4: 470_2.Pin_1, 7476.pin1, NPN_2.C, 100uF_2.+
  N5: 8_OHM.1, PNP.C, 0_05uF.0
  N6: 8_OHM.2, 0_01uF.1, 0_05uF.1
  N7: 8_OHM.3, SOUND.COM
  N8: 8_OHM.4, SPKR.pin1
  N9: 900CT.pin1, +_4_5V_-.pin1, 7400.pin7, 7476.pin13, NPN.E, NPN_2.E
  N10: 4_7K.Pin_0, 4_7K_2.Pin_0, 7400.pin14, 7476.pin2, 7476.pin3, 7476.pin4, 7476.pin5, 7476.pin7, 7476.pin8, 7476.pin9, 7476.pin12, 7476.pin16, PNP.E, POWER.COM, 144_com2.common_anode, 162_163#1.anode, 160_161#1.anode
  N11: 4_7K.Pin_1, NPN.B, 100uF_2.-
  N12: 4_7K_2.Pin_1, NPN_2.B, 100uF.-
  N13: 47K.Pin_0, PNP.B, 0_01uF.0
  N14: 47K.Pin_1, 7400.pin11
  N15: +_4_5V_-.pin2, POWER.L1
  N16: 7400.pin1, 7400.pin10, 7476.pin6, 7476.pin15, 820.Pin_0
  N17: 7400.pin2, 7476.pin11
  N18: 7400.pin3, 7400.pin4, 7400.pin5
  N19: 7400.pin6, 820_2.Pin_0, 820_4.Pin_0, 820_5.Pin_1, 820_7.Pin_1
  N20: 7400.pin8, 820_3.Pin_0, 820_6.Pin_1
  N21: 7400.pin9, 7476.pin10
  N22: 144_com2.Segment_G, 820.Pin_1
  N23: 144_com2.Segment_F, 820_2.Pin_1
  N24: 144_com2.Segment_E, 820_3.Pin_1
  N25: 144_com2.Segment_D, 820_4.Pin_1
  N26: 144_com2.Segment_C, 820_5.Pin_0
  N27: 144_com2.Segment_B, 820_6.Pin_0
  N28: 144_com2.Segment_A, 820_7.Pin_0
  N29: SPKR.pin2, SOUND.L1

notes:
  a
  b
  c
  com
  e
  d
  f
  g
  github.com/RebeccaRGB/200in1
  Miss Diode Seal of Approval
  17/200 SOS ALERT
